// Logisim project Practica2.circ as structural Verilog: 6 circuits, main circuit main
module main (
  input  in_1,
  input  in_2,
  input  in_3,
  output out_4,
  output out_5,
  output out_6
);

  wire ejercicio2_1_y_1, ejercicio2_1_y_2, ejercicio2_1_y_3, ejercicio2_1_y_4;

  Ejercicio2 ejercicio2_1 (
    .x_1(in_1), .x_2(in_2), .x_3(in_3), .y_1(ejercicio2_1_y_1), .y_2(ejercicio2_1_y_2),
    .y_3(ejercicio2_1_y_3), .y_4(ejercicio2_1_y_4));
  Ejercicio3 ejercicio3_1 (
    .y_1(ejercicio2_1_y_1), .y_2(ejercicio2_1_y_2), .y_3(ejercicio2_1_y_3), .y_4(ejercicio2_1_y_4),
    .x_1(out_4), .x_2(out_5), .x_3(out_6));
endmodule

module Ejercicio1 (
  input  D_0,
  input  D_1,
  input  D_2,
  input  D_3,
  input  D_4,
  input  D_5,
  input  D_6,
  input  D_7,
  output x,
  output y,
  output z
);

  or or_1 (x, D_4, D_5, D_6, D_7);
  or or_2 (y, D_2, D_3, D_6, D_7);
  or or_3 (z, D_1, D_3, D_5, D_7);
endmodule

module Ejercicio2 (
  input  x_1,
  input  x_2,
  input  x_3,
  output y_1,
  output y_2,
  output y_3,
  output y_4
);

  wire and_1_out, and_2_out, and_3_out, and_4_out, and_5_out, and_6_out, and_7_out, and_8_out, not_1_out,
       not_2_out, not_3_out;

  not not_1 (not_1_out, x_1);
  not not_2 (not_2_out, x_2);
  not not_3 (not_3_out, x_3);
  and and_1 (and_1_out, not_1_out, not_2_out, not_3_out);
  and and_2 (and_2_out, not_1_out, not_2_out, x_3);
  and and_3 (and_3_out, not_1_out, x_2, not_3_out);
  and and_4 (and_4_out, not_1_out, x_2, x_3);
  and and_5 (and_5_out, x_1, not_2_out, not_3_out);
  and and_6 (and_6_out, x_1, not_2_out, x_3);
  and and_7 (and_7_out, x_1, x_2, not_3_out);
  and and_8 (and_8_out, x_1, x_2, x_3);
  or or_1 (y_1, and_5_out, and_6_out, and_7_out, and_8_out);
  or or_2 (y_2, and_3_out, and_4_out, and_7_out, and_8_out);
  or or_3 (y_3, and_2_out, and_4_out, and_6_out, and_8_out);
  or or_4 (y_4, and_2_out, and_3_out, and_5_out, and_8_out);
endmodule

module Ejercicio2Min (
  input  x_1,
  input  x_2,
  input  x_3,
  output y_1,
  output y_2,
  output y_3,
  output y_4
);

  wire xor_1_out;

  xor xor_1 (xor_1_out, x_1, x_2);
  xor xor_2 (y_4, xor_1_out, x_3);

  assign y_1 = x_1;
  assign y_2 = x_2;
  assign y_3 = x_3;
endmodule

module Ejercicio3 (
  input  y_1,
  input  y_2,
  input  y_3,
  input  y_4,
  output x_1,
  output x_2,
  output x_3
);

  wire and_1_out, and_2_out, and_3_out, and_4_out, and_5_out, and_6_out, and_7_out, and_8_out, not_1_out,
       not_2_out, not_3_out, not_4_out;

  not not_1 (not_1_out, y_1);
  not not_2 (not_2_out, y_3);
  not not_3 (not_3_out, y_2);
  not not_4 (not_4_out, y_4);
  and and_1 (and_1_out, not_1_out, not_3_out, not_2_out, not_4_out);
  and and_2 (and_2_out, not_1_out, not_3_out, y_3, y_4);
  and and_3 (and_3_out, not_1_out, y_2, not_2_out, y_4);
  and and_4 (and_4_out, not_1_out, y_2, y_3, not_4_out);
  and and_5 (and_5_out, y_1, not_3_out, not_2_out, y_4);
  and and_6 (and_6_out, y_1, not_3_out, y_3, not_4_out);
  and and_7 (and_7_out, y_1, y_2, not_2_out, not_4_out);
  and and_8 (and_8_out, y_1, y_2, y_3, y_4);
  or or_1 (x_1, and_5_out, and_6_out, and_7_out, and_8_out);
  or or_2 (x_2, and_3_out, and_4_out, and_7_out, and_8_out);
  or or_3 (x_3, and_2_out, and_4_out, and_6_out, and_8_out);
endmodule

module Ejercicio4 (
  input  x_1,
  input  x_2,
  input  x_3,
  input  x_4,
  output down
);

  wire and_1_out, and_2_out, and_3_out, not_1_out, not_2_out, not_3_out, not_4_out;

  not not_1 (not_1_out, x_1);
  not not_2 (not_2_out, x_3);
  not not_3 (not_3_out, x_2);
  not not_4 (not_4_out, x_4);
  and and_1 (and_1_out, x_1, x_2, not_4_out);
  and and_2 (and_2_out, x_1, not_2_out);
  and and_3 (and_3_out, x_2, not_2_out, not_4_out);
  or or_1 (down, and_1_out, and_2_out, and_3_out);

  // Notes on the sheet:
  //   posicion
  //   llamada
endmodule
