// Logisim project Practica3.circ as structural Verilog
module sumadorMedio (
  input  x,
  input  y,
  output s,
  output c
);

  xor xor_1 (s, x, y);
  and and_1 (c, x, y);
endmodule

module sumadorCompleto1bit (
  input  x,
  input  y,
  input  c_1,
  output s,
  output c_2
);

  wire and_1_out, and_2_out, and_3_out, xor_1_out;

  xor xor_1 (xor_1_out, x, y);
  and and_1 (and_1_out, x, y);
  and and_2 (and_2_out, y, c_1);
  and and_3 (and_3_out, x, c_1);
  xor xor_2 (s, xor_1_out, c_1);
  or or_1 (c_2, and_1_out, and_2_out, and_3_out);
endmodule

module sumadorCompleto3bits (
  input  x_2,
  input  x_1,
  input  x_0,
  input  y_2,
  input  y_1,
  input  y_0,
  output c,
  output s_2,
  output s_1,
  output s_0
);

  wire sumadorcompleto1bit_2_c_2, sumadormedio_1_c;

  sumadorCompleto1bit sumadorcompleto1bit_1 (.x(x_2), .y(y_2), .c_1(sumadorcompleto1bit_2_c_2), .s(s_2), .c_2(c));
  sumadorCompleto1bit sumadorcompleto1bit_2 (
    .x(x_1), .y(y_1), .c_1(sumadormedio_1_c), .s(s_1), .c_2(sumadorcompleto1bit_2_c_2));
  sumadorMedio sumadormedio_1 (.x(x_0), .y(y_0), .s(s_0), .c(sumadormedio_1_c));

  // Notes on the sheet:
  //   +
endmodule

module restadorMedio (
  input  x,
  input  y,
  output d,
  output p
);

  wire not_1_out;

  xor xor_1 (d, x, y);
  not not_1 (not_1_out, x);
  and and_1 (p, not_1_out, y);
endmodule

module restadorCompleto1bit (
  input  x,
  input  y,
  input  p_1,
  output d,
  output p_2
);

  wire and_1_out, and_2_out, not_1_out, not_2_out, xor_1_out;

  xor xor_1 (xor_1_out, x, y);
  not not_1 (not_1_out, xor_1_out);
  and and_1 (and_1_out, not_1_out, p_1);
  not not_2 (not_2_out, x);
  and and_2 (and_2_out, not_2_out, y);
  xor xor_2 (d, xor_1_out, p_1);
  or or_1 (p_2, and_1_out, and_2_out);
endmodule

module restadorCompleto3bits (
  input  x_2,
  input  x_1,
  input  x_0,
  input  y_2,
  input  y_1,
  input  y_0,
  output p,
  output s_2,
  output s_1,
  output s_0
);

  wire restadorcompleto1bit_2_p_2, restadormedio_1_p;

  restadorCompleto1bit restadorcompleto1bit_1 (.x(x_2), .y(y_2), .p_1(restadorcompleto1bit_2_p_2), .d(s_2), .p_2(p));
  restadorCompleto1bit restadorcompleto1bit_2 (
    .x(x_1), .y(y_1), .p_1(restadormedio_1_p), .d(s_1), .p_2(restadorcompleto1bit_2_p_2));
  restadorMedio restadormedio_1 (.x(x_0), .y(y_0), .d(s_0), .p(restadormedio_1_p));

  // Notes on the sheet:
  //   -
endmodule

module Fibo (
  input  a_0,
  input  a_1,
  input  a_2,
  input  a_3,
  input  a_4,
  input  a_5,
  input  a_6,
  input  a_7,
  input  [2:0] xyz,
  output s
);

  wire decoder_1_out0, decoder_1_out1, decoder_1_out2, decoder_1_out3, decoder_1_out5, multiplexer_1_out,
       or_1_out;

  Multiplexer #(.select(3), .enable("false")) multiplexer_1 (
    .in0(a_0), .in1(a_1), .in2(a_2), .in3(a_3), .in4(a_4), .in5(a_5), .in6(a_6), .in7(a_7),
    .out(multiplexer_1_out), .sel(xyz));
  Decoder #(.select(3), .enable("false")) decoder_1 (
    .out0(decoder_1_out0), .out1(decoder_1_out1), .out2(decoder_1_out2), .out3(decoder_1_out3),
    .out5(decoder_1_out5), .sel(xyz));  // open: out4, out6, out7
  and and_1 (s, multiplexer_1_out, or_1_out);
  or or_1 (or_1_out, decoder_1_out0, decoder_1_out1, decoder_1_out2, decoder_1_out3, decoder_1_out5);
endmodule
