// Logisim project Practica4.circ as structural Verilog
module FFJK_ms (
  input  J,
  input  K,
  input  CLK,
  input  ENBL,
  output Q,
  output nQ
);

  wire and_1_out, and_2_out, j_k_ff_1_q, j_k_ff_1_qn, not_1_out;

  and and_1 (and_1_out, nQ, J);
  and and_2 (and_2_out, K, Q);
  J_K_Flip_Flop j_k_ff_1 (
    .J(and_1_out), .clk(CLK), .K(and_2_out), .Q(j_k_ff_1_q), .Qn(j_k_ff_1_qn), .en(ENBL));  // open: preset, reset
  not not_1 (not_1_out, CLK);
  J_K_Flip_Flop j_k_ff_2 (
    .J(j_k_ff_1_q), .clk(not_1_out), .K(j_k_ff_1_qn), .Q(Q), .Qn(nQ), .en(ENBL));  // open: preset, reset
endmodule

module Ejercicio1 (
  input  ENBL,
  input  CLK,
  output [6:0] O_P
);

  wire and_1_out, and_2_out, and_3_out, and_4_out, and_5_out;

  FFJK_ms ffjk_ms_1 (.J(1'b1), .K(1'b1), .CLK(CLK), .ENBL(ENBL), .Q(O_P[0]));  // open: nQ
  FFJK_ms ffjk_ms_2 (.J(O_P[0]), .K(O_P[0]), .CLK(CLK), .ENBL(ENBL), .Q(O_P[1]));  // open: nQ
  and and_1 (and_1_out, O_P[1], O_P[0]);
  FFJK_ms ffjk_ms_3 (.J(and_1_out), .K(and_1_out), .CLK(CLK), .ENBL(ENBL), .Q(O_P[2]));  // open: nQ
  and and_2 (and_2_out, O_P[2], O_P[1], O_P[0]);
  FFJK_ms ffjk_ms_4 (.J(and_2_out), .K(and_2_out), .CLK(CLK), .ENBL(ENBL), .Q(O_P[3]));  // open: nQ
  and and_3 (and_3_out, O_P[3], O_P[2], O_P[1], O_P[0]);
  and and_4 (and_4_out, O_P[4], O_P[3], O_P[2], O_P[1], O_P[0]);
  FFJK_ms ffjk_ms_5 (.J(and_3_out), .K(and_3_out), .CLK(CLK), .ENBL(ENBL), .Q(O_P[4]));  // open: nQ
  FFJK_ms ffjk_ms_6 (.J(and_4_out), .K(and_4_out), .CLK(CLK), .ENBL(ENBL), .Q(O_P[5]));  // open: nQ
  and and_5 (and_5_out, O_P[5], O_P[4], O_P[3], O_P[2], O_P[1], O_P[0]);
  FFJK_ms ffjk_ms_7 (.J(and_5_out), .K(and_5_out), .CLK(CLK), .ENBL(ENBL), .Q(O_P[6]));  // open: nQ
endmodule

module MemAux (
  input  I0,
  input  I1,
  input  I2,
  input  I3,
  input  I4,
  input  I5,
  input  I6,
  input  ENBL,
  input  CLK,
  output O0,
  output O1,
  output O2,
  output O3,
  output O4,
  output O5,
  output O6
);

  wire not_1_out;

  not not_1 (not_1_out, CLK);
  D_Flip_Flop d_ff_1 (.clk(not_1_out), .D(I0), .Q(O0), .en(ENBL));  // open: Qn, preset, reset
  D_Flip_Flop d_ff_2 (.clk(not_1_out), .D(I1), .Q(O1), .en(ENBL));  // open: Qn, preset, reset
  D_Flip_Flop d_ff_3 (.clk(not_1_out), .D(I2), .Q(O2), .en(ENBL));  // open: Qn, preset, reset
  D_Flip_Flop d_ff_4 (.clk(not_1_out), .D(I3), .Q(O3), .en(ENBL));  // open: Qn, preset, reset
  D_Flip_Flop d_ff_5 (.clk(not_1_out), .D(I4), .Q(O4), .en(ENBL));  // open: Qn, preset, reset
  D_Flip_Flop d_ff_6 (.clk(not_1_out), .D(I5), .Q(O5), .en(ENBL));  // open: Qn, preset, reset
  D_Flip_Flop d_ff_7 (.clk(not_1_out), .D(I6), .Q(O6), .en(ENBL));  // open: Qn, preset, reset
endmodule

module Ejercicio2 (
  input  ENBL
);

  wire CLK_out, memaux_1_o0, memaux_1_o1, memaux_1_o2, memaux_1_o3, memaux_1_o4, memaux_1_o5, memaux_1_o6,
       memaux_2_o0, memaux_2_o1, memaux_2_o2, memaux_2_o3, memaux_2_o4, memaux_2_o5, memaux_2_o6,
       memaux_3_o0, memaux_3_o1, memaux_3_o2, memaux_3_o3, memaux_3_o4, memaux_3_o5, memaux_3_o6,
       memaux_4_o0, memaux_4_o1, memaux_4_o2, memaux_4_o3, memaux_4_o4, memaux_4_o5, memaux_4_o6,
       memaux_5_o0, memaux_5_o1, memaux_5_o2, memaux_5_o3, memaux_5_o4, memaux_5_o5, memaux_5_o6;
  wire [6:0] ejercicio1_1_o_p, rom_1_data;

  Clock CLK (.out(CLK_out));
  Ejercicio1 ejercicio1_1 (.ENBL(ENBL), .CLK(CLK_out), .O_P(ejercicio1_1_o_p));
  MemAux memaux_1 (
    .I0(rom_1_data[0]), .I1(rom_1_data[1]), .I2(rom_1_data[2]), .I3(rom_1_data[3]), .I4(rom_1_data[4]),
    .I5(rom_1_data[5]), .I6(rom_1_data[6]), .ENBL(ENBL), .CLK(CLK_out), .O0(memaux_1_o0), .O1(memaux_1_o1),
    .O2(memaux_1_o2), .O3(memaux_1_o3), .O4(memaux_1_o4), .O5(memaux_1_o5), .O6(memaux_1_o6));
  _7_Segment_Display u_7_segment_display_1 (
    .g(memaux_1_o0), .f(memaux_1_o1), .a(memaux_1_o6), .b(memaux_1_o5), .e(memaux_1_o2), .d(memaux_1_o3),
    .c(memaux_1_o4));  // open: dp
  MemAux memaux_2 (
    .I0(memaux_1_o0), .I1(memaux_1_o1), .I2(memaux_1_o2), .I3(memaux_1_o3), .I4(memaux_1_o4),
    .I5(memaux_1_o5), .I6(memaux_1_o6), .ENBL(ENBL), .CLK(CLK_out), .O0(memaux_2_o0), .O1(memaux_2_o1),
    .O2(memaux_2_o2), .O3(memaux_2_o3), .O4(memaux_2_o4), .O5(memaux_2_o5), .O6(memaux_2_o6));
  _7_Segment_Display u_7_segment_display_2 (
    .g(memaux_2_o0), .f(memaux_2_o1), .a(memaux_2_o6), .b(memaux_2_o5), .e(memaux_2_o2), .d(memaux_2_o3),
    .c(memaux_2_o4));  // open: dp
  ROM #(.addrWidth(7), .dataWidth(7)) rom_1 (.addr(ejercicio1_1_o_p), .data(rom_1_data), .sel(ENBL));
  MemAux memaux_3 (
    .I0(memaux_2_o0), .I1(memaux_2_o1), .I2(memaux_2_o2), .I3(memaux_2_o3), .I4(memaux_2_o4),
    .I5(memaux_2_o5), .I6(memaux_2_o6), .ENBL(ENBL), .CLK(CLK_out), .O0(memaux_3_o0), .O1(memaux_3_o1),
    .O2(memaux_3_o2), .O3(memaux_3_o3), .O4(memaux_3_o4), .O5(memaux_3_o5), .O6(memaux_3_o6));
  _7_Segment_Display u_7_segment_display_3 (
    .g(memaux_3_o0), .f(memaux_3_o1), .a(memaux_3_o6), .b(memaux_3_o5), .e(memaux_3_o2), .d(memaux_3_o3),
    .c(memaux_3_o4));  // open: dp
  MemAux memaux_4 (
    .I0(memaux_3_o0), .I1(memaux_3_o1), .I2(memaux_3_o2), .I3(memaux_3_o3), .I4(memaux_3_o4),
    .I5(memaux_3_o5), .I6(memaux_3_o6), .ENBL(ENBL), .CLK(CLK_out), .O0(memaux_4_o0), .O1(memaux_4_o1),
    .O2(memaux_4_o2), .O3(memaux_4_o3), .O4(memaux_4_o4), .O5(memaux_4_o5), .O6(memaux_4_o6));
  _7_Segment_Display u_7_segment_display_4 (
    .g(memaux_4_o0), .f(memaux_4_o1), .a(memaux_4_o6), .b(memaux_4_o5), .e(memaux_4_o2), .d(memaux_4_o3),
    .c(memaux_4_o4));  // open: dp
  MemAux memaux_5 (
    .I0(memaux_4_o0), .I1(memaux_4_o1), .I2(memaux_4_o2), .I3(memaux_4_o3), .I4(memaux_4_o4),
    .I5(memaux_4_o5), .I6(memaux_4_o6), .ENBL(ENBL), .CLK(CLK_out), .O0(memaux_5_o0), .O1(memaux_5_o1),
    .O2(memaux_5_o2), .O3(memaux_5_o3), .O4(memaux_5_o4), .O5(memaux_5_o5), .O6(memaux_5_o6));
  _7_Segment_Display u_7_segment_display_5 (
    .g(memaux_5_o0), .f(memaux_5_o1), .a(memaux_5_o6), .b(memaux_5_o5), .e(memaux_5_o2), .d(memaux_5_o3),
    .c(memaux_5_o4));  // open: dp

  // Notes on the sheet:
  //   contents of rom_1 (hex, n*v repeats v):
  //   65*0 77 1f 4e 3d 4f 47 7b 37 6 3c 0 e 0 15 7e 67 73 5 5b 0 3e 0 0 0 3b
endmodule

module Ejercicio3 (
  input  I_P,
  input  ENBL,
  input  CLK,
  output O_P
);

  wire not_1_out;
  wire [5:0] rom_1_data;
  wire [5:1] d_ff_5_q;

  not not_1 (not_1_out, CLK);
  D_Flip_Flop d_ff_1 (.clk(not_1_out), .D(rom_1_data[5]), .Q(d_ff_5_q[5]), .en(ENBL));  // open: Qn, preset, reset
  D_Flip_Flop d_ff_2 (.clk(not_1_out), .D(rom_1_data[4]), .Q(d_ff_5_q[4]), .en(ENBL));  // open: Qn, preset, reset
  D_Flip_Flop d_ff_3 (.clk(not_1_out), .D(rom_1_data[3]), .Q(d_ff_5_q[3]), .en(ENBL));  // open: Qn, preset, reset
  ROM #(.addrWidth(6), .dataWidth(6)) rom_1 (.addr({d_ff_5_q, I_P}), .data(rom_1_data), .sel(ENBL));
  D_Flip_Flop d_ff_4 (.clk(not_1_out), .D(rom_1_data[2]), .Q(d_ff_5_q[2]), .en(ENBL));  // open: Qn, preset, reset
  D_Flip_Flop d_ff_5 (.clk(not_1_out), .D(rom_1_data[1]), .Q(d_ff_5_q[1]), .en(ENBL));  // open: Qn, preset, reset
  D_Flip_Flop d_ff_6 (.clk(not_1_out), .D(rom_1_data[0]), .Q(O_P), .en(ENBL));  // open: Qn, preset, reset

  // Notes on the sheet:
  //   contents of rom_1 (hex, n*v repeats v):
  //   2 0 0 4 6 0 8 a 0 c 1a 0 e 0 10 12 15 17 19 7*0 1c 0 0 1e 0 21
endmodule

module Ejercicio3v2 (
  input  [6:0] I_P,
  input  ENBL,
  output O_P
);

  ROM #(.addrWidth(7), .dataWidth(1)) rom_1 (.addr(I_P), .data(O_P), .sel(ENBL));

  // Notes on the sheet:
  //   contents of rom_1 (hex, n*v repeats v):
  //   72*0 1 1 1 8*0 1
endmodule

module Ejercicio4 (
  input  ENBL
);

  wire and_1_out, CLK_out, ejercicio3v2_1_o_p, memaux_1_o0, memaux_1_o1, memaux_1_o2, memaux_1_o3,
       memaux_1_o4, memaux_1_o5, memaux_1_o6, memaux_2_o0, memaux_2_o1, memaux_2_o2, memaux_2_o3,
       memaux_2_o4, memaux_2_o5, memaux_2_o6, memaux_3_o0, memaux_3_o1, memaux_3_o2, memaux_3_o3,
       memaux_3_o4, memaux_3_o5, memaux_3_o6, memaux_4_o0, memaux_4_o1, memaux_4_o2, memaux_4_o3,
       memaux_4_o4, memaux_4_o5, memaux_4_o6, memaux_5_o0, memaux_5_o1, memaux_5_o2, memaux_5_o3,
       memaux_5_o4, memaux_5_o5, memaux_5_o6;
  wire [6:0] ejercicio1_1_o_p, rom_1_data;

  Clock CLK (.out(CLK_out));
  MemAux memaux_1 (
    .I0(rom_1_data[0]), .I1(rom_1_data[1]), .I2(rom_1_data[2]), .I3(rom_1_data[3]), .I4(rom_1_data[4]),
    .I5(rom_1_data[5]), .I6(rom_1_data[6]), .ENBL(ENBL), .CLK(and_1_out), .O0(memaux_1_o0), .O1(memaux_1_o1),
    .O2(memaux_1_o2), .O3(memaux_1_o3), .O4(memaux_1_o4), .O5(memaux_1_o5), .O6(memaux_1_o6));
  _7_Segment_Display u_7_segment_display_1 (
    .g(memaux_1_o0), .f(memaux_1_o1), .a(memaux_1_o6), .b(memaux_1_o5), .e(memaux_1_o2), .d(memaux_1_o3),
    .c(memaux_1_o4));  // open: dp
  Ejercicio1 ejercicio1_1 (.ENBL(ENBL), .CLK(CLK_out), .O_P(ejercicio1_1_o_p));
  MemAux memaux_2 (
    .I0(memaux_1_o0), .I1(memaux_1_o1), .I2(memaux_1_o2), .I3(memaux_1_o3), .I4(memaux_1_o4),
    .I5(memaux_1_o5), .I6(memaux_1_o6), .ENBL(ENBL), .CLK(and_1_out), .O0(memaux_2_o0), .O1(memaux_2_o1),
    .O2(memaux_2_o2), .O3(memaux_2_o3), .O4(memaux_2_o4), .O5(memaux_2_o5), .O6(memaux_2_o6));
  _7_Segment_Display u_7_segment_display_2 (
    .g(memaux_2_o0), .f(memaux_2_o1), .a(memaux_2_o6), .b(memaux_2_o5), .e(memaux_2_o2), .d(memaux_2_o3),
    .c(memaux_2_o4));  // open: dp
  ROM #(.addrWidth(7), .dataWidth(7)) rom_1 (.addr(ejercicio1_1_o_p), .data(rom_1_data), .sel(ENBL));
  Ejercicio3v2 ejercicio3v2_1 (.I_P(ejercicio1_1_o_p), .ENBL(ENBL), .O_P(ejercicio3v2_1_o_p));
  and and_1 (and_1_out, CLK_out, ejercicio3v2_1_o_p);
  MemAux memaux_3 (
    .I0(memaux_2_o0), .I1(memaux_2_o1), .I2(memaux_2_o2), .I3(memaux_2_o3), .I4(memaux_2_o4),
    .I5(memaux_2_o5), .I6(memaux_2_o6), .ENBL(ENBL), .CLK(and_1_out), .O0(memaux_3_o0), .O1(memaux_3_o1),
    .O2(memaux_3_o2), .O3(memaux_3_o3), .O4(memaux_3_o4), .O5(memaux_3_o5), .O6(memaux_3_o6));
  _7_Segment_Display u_7_segment_display_3 (
    .g(memaux_3_o0), .f(memaux_3_o1), .a(memaux_3_o6), .b(memaux_3_o5), .e(memaux_3_o2), .d(memaux_3_o3),
    .c(memaux_3_o4));  // open: dp
  MemAux memaux_4 (
    .I0(memaux_3_o0), .I1(memaux_3_o1), .I2(memaux_3_o2), .I3(memaux_3_o3), .I4(memaux_3_o4),
    .I5(memaux_3_o5), .I6(memaux_3_o6), .ENBL(ENBL), .CLK(and_1_out), .O0(memaux_4_o0), .O1(memaux_4_o1),
    .O2(memaux_4_o2), .O3(memaux_4_o3), .O4(memaux_4_o4), .O5(memaux_4_o5), .O6(memaux_4_o6));
  _7_Segment_Display u_7_segment_display_4 (
    .g(memaux_4_o0), .f(memaux_4_o1), .a(memaux_4_o6), .b(memaux_4_o5), .e(memaux_4_o2), .d(memaux_4_o3),
    .c(memaux_4_o4));  // open: dp
  MemAux memaux_5 (
    .I0(memaux_4_o0), .I1(memaux_4_o1), .I2(memaux_4_o2), .I3(memaux_4_o3), .I4(memaux_4_o4),
    .I5(memaux_4_o5), .I6(memaux_4_o6), .ENBL(ENBL), .CLK(and_1_out), .O0(memaux_5_o0), .O1(memaux_5_o1),
    .O2(memaux_5_o2), .O3(memaux_5_o3), .O4(memaux_5_o4), .O5(memaux_5_o5), .O6(memaux_5_o6));
  _7_Segment_Display u_7_segment_display_5 (
    .g(memaux_5_o0), .f(memaux_5_o1), .a(memaux_5_o6), .b(memaux_5_o5), .e(memaux_5_o2), .d(memaux_5_o3),
    .c(memaux_5_o4));  // open: dp

  // Notes on the sheet:
  //   contents of rom_1 (hex, n*v repeats v):
  //   65*0 77 1f 4e 3d 4f 47 7b 37 6 3c 0 e 0 15 7e 67 73 5 5b 0 3e 0 0 0 3b
endmodule
